# Fritzing sketch NanoRGB3POTs (saved by Fritzing 0.9.9b)
breadboards: 1

parts:
  Part1 = Arduino Nano (Rev3.0)
  LED1 = RGB LED (com. cathode, rgb) [package="5 mm [THT]"]
  R1 = Resistor [tolerance=±5% power=0.25 resistance=220 package=THT]
  R2 = Resistor [tolerance=±5% power=0.25 resistance=220 package=THT]
  R3 = Resistor [tolerance=±5% power=0.25 resistance=220 package=THT]
  R4 = Rotary Potentiometer (Small) [maximum_resistance=100kΩ package=THT]
  R5 = Rotary Potentiometer (Small) [maximum_resistance=100kΩ package=THT]
  R6 = Rotary Potentiometer (Small) [maximum_resistance=100kΩ package=THT]

nets:
  N1: Part1.GND, R1.Pin_1, R2.Pin_1, R3.Pin_1, R4.leg2, R5.leg2, R6.leg2
  N2: Part1.D9, LED1.red_anode, R1.Pin_0
  N3: Part1.D10, LED1.green_anode, R2.Pin_0
  N4: Part1.D11/MOSI, LED1.blue_anode, R3.Pin_0
  N5: Part1.5V, LED1.common_cathode, R4.leg1, R5.leg1, R6.leg1
  N6: Part1.A2, R6.wiper
  N7: Part1.A1, R5.wiper
  N8: Part1.A0, R4.wiper
